// Logisim project control-logic.circ as structural Verilog: 1 circuit, main circuit control_logic
module control_logic (
  input  [31:0] Instruction,
  input  BrEq,
  input  BrLt,
  output PCSel,
  output RegWEn,
  output [2:0] ImmSel,
  output BrUn,
  output ASel,
  output BSel,
  output [3:0] ALUSel,
  output MemWEn,
  output [1:0] WBSel
);

  wire and_4_out, and_5_out, and_6_out, and_7_out, and_8_out, and_9_out, comparator_1_eq, comparator_2_eq,
       comparator_3_eq, comparator_4_eq, comparator_5_eq, comparator_6_eq, comparator_7_eq, comparator_8_eq,
       comparator_9_eq, comparator_10_eq, comparator_11_eq, comparator_12_eq, comparator_13_eq,
       comparator_14_eq, comparator_15_eq, comparator_16_eq, comparator_17_eq, comparator_18_eq,
       comparator_19_eq, comparator_20_eq, comparator_21_eq, comparator_22_eq, comparator_23_eq,
       comparator_24_eq, comparator_25_eq, comparator_26_eq, comparator_27_eq, comparator_28_eq,
       comparator_29_eq, comparator_30_eq, comparator_31_eq, comparator_33_eq, comparator_34_eq,
       comparator_35_eq, comparator_36_eq, comparator_37_eq, comparator_38_eq, comparator_39_eq,
       comparator_40_eq, comparator_41_eq, comparator_42_eq, comparator_43_eq, comparator_44_eq,
       comparator_45_eq, comparator_46_eq, comparator_47_eq, comparator_48_eq, comparator_49_eq,
       comparator_52_eq, comparator_53_eq, comparator_55_eq, comparator_56_eq, ImmSel_B, ImmSel_J, ImmSel_U,
       is_mul, is_mulh, is_mulhu, is_sra, is_sub, not_1_out, not_2_out, not_3_out, or_4_out, or_5_out,
       or_7_out, or_11_out, WBSel_ALU, WBSel_PC_4;
  wire [1:0] multiplexer_3_out;
  wire [2:0] multiplexer_10_out, multiplexer_11_out, multiplexer_13_out;
  wire [3:0] multiplexer_1_out, multiplexer_2_out, multiplexer_4_out, multiplexer_6_out, multiplexer_7_out,
       multiplexer_9_out, RISel;

  Multiplexer #(.enable("false"), .select(3), .width(4)) multiplexer_1 (
    .in0(4'b0000), .in1(4'b0001), .in2(4'b0010), .in4(4'b0100), .in5(4'b0101), .in6(4'b0110), .in7(4'b0111),
    .out(multiplexer_1_out), .sel(Instruction[14:12]));  // open: in3
  Multiplexer #(.enable("false"), .width(4)) multiplexer_2 (
    .in0(multiplexer_1_out), .in1(4'b1000), .out(multiplexer_2_out), .sel(is_mul));
  Comparator #(.width(7)) comparator_1 (.a(Instruction[6:0]), .b(7'b0110011), .eq(comparator_1_eq));  // open: gt, lt
  Comparator #(.width(7)) comparator_2 (.a(Instruction[6:0]), .b(7'b0000011), .eq(comparator_2_eq));  // open: gt, lt
  Comparator #(.width(7)) comparator_3 (.a(Instruction[6:0]), .b(7'b0010011), .eq(comparator_3_eq));  // open: gt, lt
  Comparator #(.width(7)) comparator_4 (.a(Instruction[6:0]), .b(7'b1100111), .eq(comparator_4_eq));  // open: gt, lt
  Comparator #(.width(7)) comparator_5 (.a(Instruction[6:0]), .b(7'b0010111), .eq(comparator_5_eq));  // open: gt, lt
  Comparator #(.width(7)) comparator_6 (.a(Instruction[6:0]), .b(7'b0110111), .eq(comparator_6_eq));  // open: gt, lt
  Comparator #(.width(7)) comparator_7 (.a(Instruction[6:0]), .b(7'b1101111), .eq(comparator_7_eq));  // open: gt, lt
  Comparator #(.width(7)) comparator_8 (.a(Instruction[6:0]), .b(7'b1100011), .eq(comparator_8_eq));  // open: gt, lt
  Comparator #(.width(3)) comparator_9 (.a(Instruction[14:12]), .b(3'b000), .eq(comparator_9_eq));  // open: gt, lt
  Comparator #(.width(3)) comparator_10 (.a(Instruction[14:12]), .b(3'b001), .eq(comparator_10_eq));  // open: gt, lt
  Comparator #(.width(3)) comparator_11 (.a(Instruction[14:12]), .b(3'b100), .eq(comparator_11_eq));  // open: gt, lt
  Comparator #(.width(3)) comparator_12 (.a(Instruction[14:12]), .b(3'b101), .eq(comparator_12_eq));  // open: gt, lt
  Comparator #(.width(3)) comparator_13 (.a(Instruction[14:12]), .b(3'b110), .eq(comparator_13_eq));  // open: gt, lt
  Comparator #(.width(3)) comparator_14 (.a(Instruction[14:12]), .b(3'b111), .eq(comparator_14_eq));  // open: gt, lt
  Comparator #(.width(7)) comparator_15 (.a(Instruction[6:0]), .b(7'b0110011), .eq(comparator_15_eq));  // open: gt, lt
  Comparator #(.width(7)) comparator_16 (.a(Instruction[6:0]), .b(7'b0010011), .eq(comparator_16_eq));  // open: gt, lt
  Comparator #(.width(7)) comparator_17 (.a(Instruction[6:0]), .b(7'b0010111), .eq(comparator_17_eq));  // open: gt, lt
  Comparator #(.width(7)) comparator_18 (.a(Instruction[6:0]), .b(7'b0110111), .eq(comparator_18_eq));  // open: gt, lt
  Comparator #(.width(7)) comparator_19 (.a(Instruction[6:0]), .b(7'b1100111), .eq(comparator_19_eq));  // open: gt, lt
  Comparator #(.width(7)) comparator_20 (.a(Instruction[6:0]), .b(7'b1101111), .eq(comparator_20_eq));  // open: gt, lt
  Multiplexer #(.enable("false"), .width(2)) multiplexer_3 (
    .in0(2'b00), .in1(2'b01), .out(multiplexer_3_out), .sel(WBSel_ALU));
  Multiplexer #(.enable("false"), .width(4)) multiplexer_4 (
    .in0(multiplexer_2_out), .in1(4'b1001), .out(multiplexer_4_out), .sel(is_mulh));
  Multiplexer #(.enable("false"), .width(2)) multiplexer_5 (
    .in0(multiplexer_3_out), .in1(2'b10), .out(WBSel), .sel(WBSel_PC_4));
  Multiplexer #(.enable("false"), .width(4)) multiplexer_6 (
    .in0(multiplexer_4_out), .in1(4'b1011), .out(multiplexer_6_out), .sel(is_mulhu));
  Comparator #(.width(7)) comparator_21 (.a(Instruction[6:0]), .b(7'b0110011), .eq(comparator_21_eq));  // open: gt, lt
  Comparator #(.width(3)) comparator_22 (.a(Instruction[14:12]), .b(3'b000), .eq(comparator_22_eq));  // open: gt, lt
  Comparator #(.width(7)) comparator_23 (
    .a(Instruction[31:25]), .b(7'b0000001), .eq(comparator_23_eq));  // open: gt, lt
  Comparator #(.width(7)) comparator_24 (.a(Instruction[6:0]), .b(7'b0110011), .eq(comparator_24_eq));  // open: gt, lt
  Comparator #(.width(3)) comparator_25 (.a(Instruction[14:12]), .b(3'b001), .eq(comparator_25_eq));  // open: gt, lt
  Comparator #(.width(7)) comparator_26 (
    .a(Instruction[31:25]), .b(7'b0000001), .eq(comparator_26_eq));  // open: gt, lt
  Comparator #(.width(7)) comparator_27 (.a(Instruction[6:0]), .b(7'b0110011), .eq(comparator_27_eq));  // open: gt, lt
  Comparator #(.width(3)) comparator_28 (.a(Instruction[14:12]), .b(3'b011), .eq(comparator_28_eq));  // open: gt, lt
  Comparator #(.width(7)) comparator_29 (
    .a(Instruction[31:25]), .b(7'b0000001), .eq(comparator_29_eq));  // open: gt, lt
  or or_1 (RegWEn, comparator_1_eq, comparator_2_eq, comparator_3_eq, comparator_4_eq, comparator_5_eq, comparator_6_eq, comparator_7_eq);
  not not_1 (not_1_out, BrEq);
  not not_2 (not_2_out, BrLt);
  not not_3 (not_3_out, BrLt);
  or or_2 (WBSel_ALU, comparator_15_eq, comparator_16_eq, comparator_17_eq, comparator_18_eq);
  or or_3 (WBSel_PC_4, comparator_19_eq, comparator_20_eq);
  Multiplexer #(.enable("false"), .width(4)) multiplexer_7 (
    .in0(multiplexer_6_out), .in1(4'b1100), .out(multiplexer_7_out), .sel(is_sub));
  and and_1 (is_mul, comparator_21_eq, comparator_22_eq, comparator_23_eq);
  and and_2 (is_mulh, comparator_24_eq, comparator_25_eq, comparator_26_eq);
  and and_3 (is_mulhu, comparator_27_eq, comparator_28_eq, comparator_29_eq);
  and and_4 (and_4_out, comparator_8_eq, comparator_9_eq, BrEq);
  and and_5 (and_5_out, comparator_8_eq, comparator_10_eq, not_1_out);
  and and_6 (and_6_out, comparator_8_eq, comparator_11_eq, BrLt);
  and and_7 (and_7_out, comparator_8_eq, comparator_12_eq, not_2_out);
  and and_8 (and_8_out, comparator_8_eq, comparator_13_eq, BrLt);
  and and_9 (and_9_out, comparator_8_eq, comparator_14_eq, not_3_out);
  Comparator #(.width(7)) comparator_30 (.a(Instruction[6:0]), .b(7'b1100111), .eq(comparator_30_eq));  // open: gt, lt
  Comparator #(.width(7)) comparator_31 (.a(Instruction[6:0]), .b(7'b1101111), .eq(comparator_31_eq));  // open: gt, lt
  Multiplexer #(.enable("false"), .width(4)) multiplexer_8 (
    .in0(multiplexer_7_out), .in1(4'b1101), .out(RISel), .sel(is_sra));
  or or_4 (or_4_out, and_4_out, and_5_out, and_6_out, and_7_out, and_8_out, and_9_out);
  or or_5 (or_5_out, comparator_30_eq, comparator_31_eq);
  or or_6 (PCSel, or_4_out, or_5_out);
  Comparator #(.width(7)) comparator_32 (.a(Instruction[6:0]), .b(7'b0100011));  // open: gt, eq, lt
  Comparator #(.width(7)) comparator_33 (.a(Instruction[6:0]), .b(7'b0000011), .eq(comparator_33_eq));  // open: gt, lt
  Comparator #(.width(7)) comparator_34 (.a(Instruction[6:0]), .b(7'b0010011), .eq(comparator_34_eq));  // open: gt, lt
  Comparator #(.width(7)) comparator_35 (.a(Instruction[6:0]), .b(7'b0010111), .eq(comparator_35_eq));  // open: gt, lt
  Comparator #(.width(7)) comparator_36 (.a(Instruction[6:0]), .b(7'b0110111), .eq(comparator_36_eq));  // open: gt, lt
  Comparator #(.width(7)) comparator_37 (.a(Instruction[6:0]), .b(7'b1100011), .eq(comparator_37_eq));  // open: gt, lt
  Comparator #(.width(7)) comparator_38 (.a(Instruction[6:0]), .b(7'b1101111), .eq(comparator_38_eq));  // open: gt, lt
  Comparator #(.width(7)) comparator_39 (.a(Instruction[6:0]), .b(7'b1100111), .eq(comparator_39_eq));  // open: gt, lt
  Comparator #(.width(7)) comparator_40 (.a(Instruction[6:0]), .b(7'b0110011), .eq(comparator_40_eq));  // open: gt, lt
  Comparator #(.width(7)) comparator_41 (.a(Instruction[6:0]), .b(7'b0010011), .eq(comparator_41_eq));  // open: gt, lt
  Comparator #(.width(7)) comparator_42 (.a(Instruction[6:0]), .b(7'b0110011), .eq(comparator_42_eq));  // open: gt, lt
  Comparator #(.width(3)) comparator_43 (.a(Instruction[14:12]), .b(3'b000), .eq(comparator_43_eq));  // open: gt, lt
  Comparator #(.width(7)) comparator_44 (
    .a(Instruction[31:25]), .b(7'b0100000), .eq(comparator_44_eq));  // open: gt, lt
  Comparator #(.width(3)) comparator_45 (.a(Instruction[14:12]), .b(3'b101), .eq(comparator_45_eq));  // open: gt, lt
  Comparator #(.width(7)) comparator_46 (
    .a(Instruction[31:25]), .b(7'b0100000), .eq(comparator_46_eq));  // open: gt, lt
  Comparator #(.width(7)) comparator_47 (.a(Instruction[6:0]), .b(7'b1101111), .eq(comparator_47_eq));  // open: gt, lt
  Comparator #(.width(7)) comparator_48 (.a(Instruction[6:0]), .b(7'b0010111), .eq(comparator_48_eq));  // open: gt, lt
  or or_7 (or_7_out, comparator_40_eq, comparator_41_eq);
  and and_10 (is_sub, comparator_42_eq, comparator_43_eq, comparator_44_eq);
  and and_11 (is_sra, comparator_45_eq, comparator_46_eq);
  or or_8 (BSel, comparator_33_eq, comparator_34_eq, comparator_35_eq, comparator_36_eq, comparator_37_eq, comparator_38_eq, comparator_39_eq);
  Multiplexer #(.enable("false"), .width(4)) multiplexer_9 (
    .in0(4'b0000), .in1(RISel), .out(multiplexer_9_out), .sel(or_7_out));
  or or_9 (ASel, comparator_8_eq, comparator_47_eq, comparator_48_eq);
  Multiplexer #(.enable("false"), .width(3)) multiplexer_10 (
    .in0(3'b000), .in1(3'b001), .out(multiplexer_10_out), .sel(MemWEn));
  Comparator #(.width(7)) comparator_49 (.a(Instruction[6:0]), .b(7'b0110111), .eq(comparator_49_eq));  // open: gt, lt
  Multiplexer #(.enable("false"), .width(3)) multiplexer_11 (
    .in0(multiplexer_10_out), .in1(3'b010), .out(multiplexer_11_out), .sel(ImmSel_B));
  Multiplexer #(.enable("false"), .width(4)) multiplexer_12 (
    .in0(multiplexer_9_out), .in1(4'b1111), .out(ALUSel), .sel(comparator_49_eq));
  Comparator #(.width(7)) comparator_50 (.a(Instruction[6:0]), .b(7'b0100011), .eq(MemWEn));  // open: gt, lt
  Comparator #(.width(7)) comparator_51 (.a(Instruction[6:0]), .b(7'b1100011), .eq(ImmSel_B));  // open: gt, lt
  Comparator #(.width(7)) comparator_52 (.a(Instruction[6:0]), .b(7'b0010111), .eq(comparator_52_eq));  // open: gt, lt
  Comparator #(.width(7)) comparator_53 (.a(Instruction[6:0]), .b(7'b0110111), .eq(comparator_53_eq));  // open: gt, lt
  Comparator #(.width(7)) comparator_54 (.a(Instruction[6:0]), .b(7'b1101111), .eq(ImmSel_J));  // open: gt, lt
  Multiplexer #(.enable("false"), .width(3)) multiplexer_13 (
    .in0(multiplexer_11_out), .in1(3'b011), .out(multiplexer_13_out), .sel(ImmSel_U));
  or or_10 (ImmSel_U, comparator_52_eq, comparator_53_eq);
  Multiplexer #(.enable("false"), .width(3)) multiplexer_14 (
    .in0(multiplexer_13_out), .in1(3'b100), .out(ImmSel), .sel(ImmSel_J));
  Comparator #(.width(3)) comparator_55 (.a(Instruction[14:12]), .b(3'b110), .eq(comparator_55_eq));  // open: gt, lt
  Comparator #(.width(3)) comparator_56 (.a(Instruction[14:12]), .b(3'b111), .eq(comparator_56_eq));  // open: gt, lt
  or or_11 (or_11_out, comparator_55_eq, comparator_56_eq);
  and and_12 (BrUn, ImmSel_B, or_11_out);

  // Other names for the same wires on the sheet: ImmSel_S = MemWEn; opcode[6:0] = Instruction[6:0];
  //   rd[4:0] = Instruction[11:7]; funct3[2:0] = Instruction[14:12]; rs1[4:0] = Instruction[19:15];
  //   rs2[4:0] = Instruction[24:20]; funct7[6:0] = Instruction[31:25]

  // Notes on the sheet:
  //   add
  //   sll
  //   slt
  //   xor
  //   srl
  //   or
  //   and
  //   Branch
  //   beq
  //   bne
  //   blt
  //   bge
  //   bltu
  //   bgeu
  //   R-type
  //   I-type
  //   auipc
  //   lui
  //   jalr
  //   jal
  //   INPUTS to your circuit
  //   R-type
  //   I-type
  //   U-type
  //   J-type
  //   RegWEn
  //   jalr
  //   jal
  //   func3 value correspond to these command directly
  //   WBSel
  //   PCSel(0->PC+4, 1->ALU)
  //   DON'T CHANGE THE LOCATIONS OF THE INPUTS AND OUTPUTS!
  //   ALUSel
  //   We separately identify the command mul, mulh, mulhu, sub and sra
  //   Note: lui use the bsel control logic of ALU so it sitll belongs to ALU
  //   OUTPUT from your circuit
  //   BSel(0->rs2, 1->imm)
  //   jal
  //   auipc
  //   R-Instruction
  //   I-Instruction
  //   ASel(0->rs1, 1->PC)
  //   Decode
  //   Except R and I instructions, other instruction all use add
  //   S-type
  //   B-type
  //   U-type
  //   S-type
  //   0b000 is I-type
  //   lui
  //   ImmSel
  //   Only S-type needs to write memory
  //   MemWEn
  //   BrUn
endmodule
