// Logisim project imm-gen.circ as structural Verilog: 1 circuit, main circuit imm_gen
module imm_gen (
  input  [31:0] Instruction,
  input  [2:0] ImmSel,
  output [31:0] Immediate
);

  Multiplexer #(.enable("false"), .select(3), .width(32)) multiplexer_1 (
    .in0({{20{1'b0}}, Instruction[31:20]}), .in1({{20{1'b0}}, Instruction[31:25], Instruction[11:7]}),
    .in2({{19{1'b0}}, Instruction[31], Instruction[7], Instruction[30:25], Instruction[11:8], 1'b0}),
    .in3({Instruction[31:12], {12{1'b0}}}),
    .in4({{11{1'b0}}, Instruction[20:12], Instruction[20], Instruction[30:21], 1'b0}), .out(Immediate),
    .sel(ImmSel));  // open: in5, in6, in7

  // Other names for the same wires on the sheet: B_type[12:1] = {Instruction[31], Instruction[7], Instruction[30:25], Instruction[11:8]};
  //   S_type[11:0] = {Instruction[31:25], Instruction[11:7]}; B_bit7 = Instruction[7];
  //   J_bit12_19[7:0] = Instruction[19:12]; J_type[20:1] = {Instruction[20:12], Instruction[20], Instruction[30:21]};
  //   U_type[31:12] = Instruction[31:12]; I_type[11:0] = Instruction[31:20]; J_bit20 = Instruction[20];
  //   J_bit21_30[9:0] = Instruction[30:21]; J_bit31 = Instruction[31]

  // Notes on the sheet:
  //   INPUTS to your circuit
  //   DON'T CHANGE THE LOCATIONS OF THE INPUTS AND OUTPUTS!
  //   OUTPUT from your circuit
endmodule
