// Logisim project alu-mult.circ as structural Verilog: 1 circuit, main circuit main
module main (
  output [7:0] Test,
  output [31:0] ALUResult,
  output halt,
  output [31:0] InputA,
  output [31:0] InputB,
  output [3:0] ALUSel
);

  wire clock_1_out;
  wire [7:0] adder_1_out;

  Clock clock_1 (.out(clock_1_out));
  Adder adder_1 (.a(8'h1), .b(Test), .out(adder_1_out));  // open: cin, cout
  Register register_1 (.D(adder_1_out), .clk(clock_1_out), .Q(Test));  // open: en, clr
  ROM #(.dataWidth(32)) rom_1 (.addr(Test), .data(InputA));
  Comparator comparator_1 (.a(Test), .b(8'h11), .eq(halt));  // open: gt, lt
  // Probe on InputB
  ROM #(.dataWidth(32)) rom_2 (.addr(Test), .data(InputB));
  // Probe on ALUSel
  // Probe on InputA
  alu alu_1 (.ALUResult(ALUResult), .A(InputA), .B(InputB), .ALUSel(ALUSel));
  ROM #(.dataWidth(4)) rom_3 (.addr(Test), .data(ALUSel));

  // Notes on the sheet:
  //   contents of rom_1 (hex, n*v repeats v):
  //   123 7435daa4 ffffdead efffffff 10 10000 123 7435daa4 ffffdead efffffff 10 10000 123 7435daa4
  //   ffffdead efffffff 10 10000
  //   Your ALU must fit here!
  //   contents of rom_2 (hex, n*v repeats v):
  //   155 62381add ffffbeef ac273deb f0000000 10000 155 62381add ffffbeef ac273deb f0000000 10000 155
  //   62381add ffffbeef ac273deb f0000000 10000
  //   There should be no red or blue wires, and the result should not be all X's
  //   contents of rom_3 (hex, n*v repeats v):
  //   8 8 8 8 8 8 b b b b b b 9 9 9 9 9 9
endmodule
