// Logisim project partial-load-half.circ as structural Verilog: 1 circuit, main circuit main
module main (
  output [7:0] Test,
  output [31:0] DataToReg,
  output halt,
  output [31:0] Instruction,
  output [31:0] MemAddress,
  output [31:0] DataFromMem
);

  wire clock_1_out;
  wire [7:0] adder_1_out;

  Clock clock_1 (.out(clock_1_out));
  Adder adder_1 (.a(8'h1), .b(Test), .out(adder_1_out));  // open: cin, cout
  Register register_1 (.D(adder_1_out), .clk(clock_1_out), .Q(Test));  // open: en, clr
  ROM #(.dataWidth(32)) rom_1 (.addr(Test), .data(Instruction));
  Comparator comparator_1 (.a(Test), .b(8'hc), .eq(halt));  // open: gt, lt
  // Probe on MemAddress
  // Probe on Instruction
  // Probe on DataFromMem
  ROM #(.dataWidth(32)) rom_2 (.addr(Test), .data(MemAddress));
  partial_load partial_load_1 (
    .Instruction(Instruction), .MemAddress(MemAddress), .DataFromMem(DataFromMem), .DataToReg(DataToReg));
  ROM #(.dataWidth(32)) rom_3 (.addr(Test), .data(DataFromMem));

  // Notes on the sheet:
  //   contents of rom_1 (hex, n*v repeats v):
  //   59503 259503 59503 259503  49403 249403 49403 249403  459503 659503 659503 459503
  //   partial_load must fit here!
  //   contents of rom_2 (hex, n*v repeats v):
  //   61c061c0 61c061c2 deadbeec deadbeee 61c061c0 61c061c2 deadbeec deadbeee 61c061c0 61c061c2 deadbeec
  //   deadbeee
  //   There should be no red or blue wires, and the result should not be all X's
  //   contents of rom_3 (hex, n*v repeats v):
  //   deadbeef deadbeef 12345678 12345678 deadbeef deadbeef 12345678 12345678 deadbeef deadbeef 12345678
  //   12345678
endmodule
