// Logisim project partial-store-word.circ as structural Verilog: 1 circuit, main circuit main
module main (
  output [7:0] Test,
  output [3:0] MemWriteMask,
  output [31:0] DataToMem,
  output halt,
  output [31:0] Instruction,
  output [31:0] MemAddress,
  output [31:0] DataFromReg,
  output MemWEn
);

  wire clock_1_out;
  wire [7:0] adder_1_out;

  Clock clock_1 (.out(clock_1_out));
  Adder adder_1 (.a(8'h1), .b(Test), .out(adder_1_out));  // open: cin, cout
  Register register_1 (.D(adder_1_out), .clk(clock_1_out), .Q(Test));  // open: en, clr
  ROM #(.dataWidth(32)) rom_1 (.addr(Test), .data(Instruction));
  Comparator comparator_1 (.a(Test), .b(8'h6), .eq(halt));  // open: gt, lt
  // Probe on DataFromReg
  // Probe on Instruction
  // Probe on MemAddress
  ROM #(.dataWidth(32)) rom_2 (.addr(Test), .data(MemAddress));
  // Probe on MemWEn
  partial_store partial_store_1 (
    .Instruction(Instruction), .MemAddress(MemAddress), .DataFromReg(DataFromReg), .MemWEn(MemWEn),
    .MemWriteMask(MemWriteMask), .DataToMem(DataToMem));
  ROM #(.dataWidth(32)) rom_3 (.addr(Test), .data(DataFromReg));
  ROM #(.dataWidth(1)) rom_4 (.addr(Test));  // open: data

  // Notes on the sheet:
  //   contents of rom_1 (hex, n*v repeats v):
  //   A5A023 A5A023 84A023 84A023 A5A223 A5A223
  //   partial_store must fit here!
  //   contents of rom_2 (hex, n*v repeats v):
  //   61c061c0 deadbeec 61c061c0 deadbeec 61c061c0 deadbeec
  //   There should be no red or blue wires, and the result should not be all X's
  //   contents of rom_3 (hex, n*v repeats v):
  //   deadbeef 12345678 deadbeef 12345678 deadbeef 12345678
  //   contents of rom_4 (hex, n*v repeats v):
  //   1 1 1 1 1 1
endmodule
