// Logisim project regfile-more-regs.circ as structural Verilog: 1 circuit, main circuit main
module main (
  output [7:0] Test,
  output [31:0] ra,
  output [31:0] sp,
  output [31:0] t0,
  output [31:0] t1,
  output [31:0] t2,
  output [31:0] s0,
  output [31:0] s1,
  output [31:0] a0,
  output halt,
  output [31:0] RegReadData1,
  output [31:0] RegReadData2,
  output [4:0] ReadReg1,
  output [4:0] ReadReg2,
  output [4:0] WriteReg,
  output RegWEn,
  output [31:0] RegWriteData
);

  wire clk;
  wire [7:0] adder_1_out;

  Clock clock_1 (.out(clk));
  ROM #(.dataWidth(16)) rs1_rs2_rd_RegWEn (.addr(Test), .data({RegWEn, WriteReg, ReadReg2, ReadReg1}));
  Register register_1 (.D(adder_1_out), .clk(clk), .Q(Test));  // open: en, clr
  Adder adder_1 (.a(8'h1), .b(Test), .out(adder_1_out));  // open: cin, cout
  ROM #(.dataWidth(32)) Write_Data (.addr(Test), .data(RegWriteData));
  Comparator comparator_1 (.a(Test), .b(8'hb), .eq(halt));  // open: gt, lt
  regfile regfile_1 (
    .ReadReg1(ReadReg1), .ReadReg2(ReadReg2), .WriteReg(WriteReg), .RegWriteData(RegWriteData),
    .RegWEn(RegWEn), .clk(clk), .ra(ra), .sp(sp), .t0(t0), .t1(t1), .t2(t2), .s0(s0), .s1(s1), .a0(a0),
    .RegReadData1(RegReadData1), .RegReadData2(RegReadData2));

  // Other names for the same wires on the sheet: RFIn[15:0] = {RegWEn, WriteReg, ReadReg2, ReadReg1}

  // Notes on the sheet:
  //   contents of rs1_rs2_rd_RegWEn (hex, n*v repeats v):
  //   84a2 88a1 9422 9845 9ca6 a0c7 a4e8 a909 912a fd44 d09f 3f4
  //   contents of Write_Data (hex, n*v repeats v):
  //   ffffbeef dad fffff00d 5678 afdfadf ffffffff a786adc2 98a09723 df89a0ae 28888292 0 0
  //   Your RegFile must fit here!
  //   There should be no red or blue wires, and the result should not be all X's
endmodule
